// Logisim project source.circ as structural Verilog: 10 circuits, main circuit main
// wire3
module main (
  input  RST
);

  wire _1, _2, _3, _4, _5, _6, _7, _8, _9, _10, _11, _12, _13, _14, _15, _16, lan1, lan2, lan3, lan4, lan5,
       lan6, lan7, lan8, lan9, lan10, lan11, lan12, lan13, lan14, lan15, lan16, process_1_out_18,
       process_1_out_19, process_1_out_20, process_1_out_21, process_1_out_22, process_1_out_23,
       process_1_out_24, process_1_out_25, process_1_out_26, process_1_out_27, process_1_out_28,
       process_1_out_29, process_1_out_30, process_1_out_31, process_1_out_32, process_1_out_33;
  wire [15:0] bit_expand_1_out_17, bit_expand_1_out_18, bit_expand_1_out_19, bit_expand_1_out_20,
       bit_expand_1_out_21, bit_expand_1_out_22, bit_expand_1_out_23, bit_expand_1_out_24,
       bit_expand_1_out_25, bit_expand_1_out_26, bit_expand_1_out_27, bit_expand_1_out_28,
       bit_expand_1_out_29, bit_expand_1_out_30, bit_expand_1_out_31, bit_expand_1_out_32, display_1_out_5,
       display_1_out_6, display_1_out_7, display_1_out_8, display_2_out_5, display_2_out_6, display_2_out_7,
       display_2_out_8, display_3_out_5, display_3_out_6, display_3_out_7, display_3_out_8, display_4_out_5,
       display_4_out_6, display_4_out_7, display_4_out_8;

  Button button_1 (.out(_4));
  Button button_2 (.out(_3));
  Button button_3 (.out(_2));
  Button button_4 (.out(_1));
  Button button_5 (.out(_8));
  Button button_6 (.out(_7));
  Button button_7 (.out(_6));
  Button button_8 (.out(_5));
  Button button_9 (.out(_12));
  Button button_10 (.out(_11));
  Button button_11 (.out(_10));
  Button button_12 (.out(_9));
  Button button_13 (.out(_16));
  Button button_14 (.out(_15));
  Button button_15 (.out(_14));
  Button button_16 (.out(_13));
  bit_expand bit_expand_1 (
    .in_1(lan1), .in_2(lan2), .in_3(lan3), .in_4(lan4), .in_5(lan5), .in_6(lan6), .in_7(lan7), .in_8(lan8),
    .in_9(lan9), .in_10(lan10), .in_11(lan11), .in_12(lan12), .in_13(lan13), .in_14(lan14), .in_15(lan15),
    .in_16(lan16), .out_17(bit_expand_1_out_17), .out_18(bit_expand_1_out_18), .out_19(bit_expand_1_out_19),
    .out_20(bit_expand_1_out_20), .out_21(bit_expand_1_out_21), .out_22(bit_expand_1_out_22),
    .out_23(bit_expand_1_out_23), .out_24(bit_expand_1_out_24), .out_25(bit_expand_1_out_25),
    .out_26(bit_expand_1_out_26), .out_27(bit_expand_1_out_27), .out_28(bit_expand_1_out_28),
    .out_29(bit_expand_1_out_29), .out_30(bit_expand_1_out_30), .out_31(bit_expand_1_out_31),
    .out_32(bit_expand_1_out_32));
  DotMatrix #(.matrixcols(16), .matrixrows(16)) dotmatrix_1 (
    .col0(display_1_out_5), .col1(display_1_out_6), .col2(display_1_out_7), .col3(display_1_out_8),
    .col4(display_2_out_5), .col5(display_2_out_6), .col6(display_2_out_7), .col7(display_2_out_8),
    .col8(display_3_out_5), .col9(display_3_out_6), .col10(display_3_out_7), .col11(display_3_out_8),
    .col12(display_4_out_5), .col13(display_4_out_6), .col14(display_4_out_7), .col15(display_4_out_8));
  display display_1 (
    .in_1(bit_expand_1_out_17), .in_2(bit_expand_1_out_18), .in_3(bit_expand_1_out_19),
    .in_4(bit_expand_1_out_20), .out_5(display_1_out_5), .out_6(display_1_out_6), .out_7(display_1_out_7),
    .out_8(display_1_out_8));
  display display_2 (
    .in_1(bit_expand_1_out_21), .in_2(bit_expand_1_out_22), .in_3(bit_expand_1_out_23),
    .in_4(bit_expand_1_out_24), .out_5(display_2_out_5), .out_6(display_2_out_6), .out_7(display_2_out_7),
    .out_8(display_2_out_8));
  display display_3 (
    .in_1(bit_expand_1_out_25), .in_2(bit_expand_1_out_26), .in_3(bit_expand_1_out_27),
    .in_4(bit_expand_1_out_28), .out_5(display_3_out_5), .out_6(display_3_out_6), .out_7(display_3_out_7),
    .out_8(display_3_out_8));
  display display_4 (
    .in_1(bit_expand_1_out_29), .in_2(bit_expand_1_out_30), .in_3(bit_expand_1_out_31),
    .in_4(bit_expand_1_out_32), .out_5(display_4_out_5), .out_6(display_4_out_6), .out_7(display_4_out_7),
    .out_8(display_4_out_8));
  process process_1 (
    .in_1(_1), .in_2(_2), .in_3(_3), .in_4(_4), .in_5(_5), .in_6(_6), .in_7(_7), .in_8(_8), .in_9(_9),
    .in_10(_10), .in_11(_11), .in_12(_12), .in_13(_13), .in_14(_14), .in_15(_15), .in_16(_16), .in_17(RST),
    .out_18(process_1_out_18), .out_19(process_1_out_19), .out_20(process_1_out_20),
    .out_21(process_1_out_21), .out_22(process_1_out_22), .out_23(process_1_out_23),
    .out_24(process_1_out_24), .out_25(process_1_out_25), .out_26(process_1_out_26),
    .out_27(process_1_out_27), .out_28(process_1_out_28), .out_29(process_1_out_29),
    .out_30(process_1_out_30), .out_31(process_1_out_31), .out_32(process_1_out_32), .out_33(process_1_out_33));
  calculate_part1 calculate_part1_1 (
    .i1(process_1_out_18), .i2(process_1_out_19), .i3(process_1_out_20), .i4(process_1_out_21),
    .i5(process_1_out_22), .i6(process_1_out_23), .i7(process_1_out_24), .i8(process_1_out_25),
    .i9(process_1_out_26), .i10(process_1_out_27), .i11(process_1_out_28), .i12(process_1_out_29), .o1(lan1),
    .o2(lan2), .o3(lan3), .o4(lan4), .o5(lan5), .o6(lan6), .o7(lan7), .o8(lan8));
  calculate_part2 calculate_part2_1 (
    .i5(process_1_out_22), .i6(process_1_out_23), .i7(process_1_out_24), .i8(process_1_out_25),
    .i9(process_1_out_26), .i10(process_1_out_27), .i11(process_1_out_28), .i12(process_1_out_29), .o9(lan9),
    .i13(process_1_out_30), .i14(process_1_out_31), .i15(process_1_out_32), .i16(process_1_out_33),
    .o10(lan10), .o11(lan11), .o12(lan12), .o13(lan13), .o14(lan14), .o15(lan15), .o16(lan16));

  // Other names for the same wires on the sheet: SET = RST

  // Notes on the sheet:
  //   复位键（高电平有效）
  //   Please use the button below 
  //   to turn on all LED lights
  //   Lightout Game
endmodule

module expand (
  input  in_1,
  input  in_2,
  input  in_3,
  input  in_4,
  input  in_5,
  input  in_6,
  input  in_7,
  input  in_8,
  input  in_9,
  input  in_10,
  input  in_11,
  input  in_12,
  input  in_13,
  input  in_14,
  input  in_15,
  input  in_16,
  output [15:0] out_17,
  output [15:0] out_18,
  output [15:0] out_19,
  output [15:0] out_20,
  output [15:0] out_21,
  output [15:0] out_22,
  output [15:0] out_23,
  output [15:0] out_24,
  output [15:0] out_25,
  output [15:0] out_26,
  output [15:0] out_27,
  output [15:0] out_28,
  output [15:0] out_29,
  output [15:0] out_30,
  output [15:0] out_31,
  output [15:0] out_32
);


  assign out_17 = {16{in_1}};
  assign out_18 = {16{in_2}};
  assign out_19 = {16{in_3}};
  assign out_20 = {16{in_4}};
  assign out_21 = {16{in_5}};
  assign out_22 = {16{in_6}};
  assign out_23 = {16{in_7}};
  assign out_24 = {16{in_8}};
  assign out_25 = {16{in_9}};
  assign out_26 = {16{in_10}};
  assign out_27 = {16{in_11}};
  assign out_28 = {16{in_12}};
  assign out_29 = {16{in_13}};
  assign out_30 = {16{in_14}};
  assign out_31 = {16{in_15}};
  assign out_32 = {16{in_16}};
endmodule

module display (
  input  [15:0] in_1,
  input  [15:0] in_2,
  input  [15:0] in_3,
  input  [15:0] in_4,
  output [15:0] out_5,
  output [15:0] out_6,
  output [15:0] out_7,
  output [15:0] out_8
);


  assign out_5 = {in_4[15:12], in_3[15:12], in_2[15:12], in_1[15:12]};
  assign out_6 = {in_4[11:8], in_3[11:8], in_2[11:8], in_1[11:8]};
  assign out_7 = {in_4[7:4], in_3[7:4], in_2[7:4], in_1[7:4]};
  assign out_8 = {in_4[3:0], in_3[3:0], in_2[3:0], in_1[3:0]};
endmodule

module bit_expand (
  input  in_1,
  input  in_2,
  input  in_3,
  input  in_4,
  input  in_5,
  input  in_6,
  input  in_7,
  input  in_8,
  input  in_9,
  input  in_10,
  input  in_11,
  input  in_12,
  input  in_13,
  input  in_14,
  input  in_15,
  input  in_16,
  output [15:0] out_17,
  output [15:0] out_18,
  output [15:0] out_19,
  output [15:0] out_20,
  output [15:0] out_21,
  output [15:0] out_22,
  output [15:0] out_23,
  output [15:0] out_24,
  output [15:0] out_25,
  output [15:0] out_26,
  output [15:0] out_27,
  output [15:0] out_28,
  output [15:0] out_29,
  output [15:0] out_30,
  output [15:0] out_31,
  output [15:0] out_32
);


  assign out_17 = {16{in_1}};
  assign out_18 = {16{in_2}};
  assign out_19 = {16{in_3}};
  assign out_20 = {16{in_4}};
  assign out_21 = {16{in_5}};
  assign out_22 = {16{in_6}};
  assign out_23 = {16{in_7}};
  assign out_24 = {16{in_8}};
  assign out_25 = {16{in_9}};
  assign out_26 = {16{in_10}};
  assign out_27 = {16{in_11}};
  assign out_28 = {16{in_12}};
  assign out_29 = {16{in_13}};
  assign out_30 = {16{in_14}};
  assign out_31 = {16{in_15}};
  assign out_32 = {16{in_16}};
endmodule

module process (
  input  in_1,
  input  in_2,
  input  in_3,
  input  in_4,
  input  in_5,
  input  in_6,
  input  in_7,
  input  in_8,
  input  in_9,
  input  in_10,
  input  in_11,
  input  in_12,
  input  in_13,
  input  in_14,
  input  in_15,
  input  in_16,
  input  in_17,
  output out_18,
  output out_19,
  output out_20,
  output out_21,
  output out_22,
  output out_23,
  output out_24,
  output out_25,
  output out_26,
  output out_27,
  output out_28,
  output out_29,
  output out_30,
  output out_31,
  output out_32,
  output out_33
);

  Asy_D_latch asy_d_latch_1 (.RST(in_17), .CLK(in_1), .D(out_18), .nQ(out_18));  // open: Q
  Asy_D_latch asy_d_latch_2 (.RST(in_17), .CLK(in_2), .D(out_19), .nQ(out_19));  // open: Q
  Asy_D_latch asy_d_latch_3 (.RST(in_17), .CLK(in_3), .D(out_20), .nQ(out_20));  // open: Q
  Asy_D_latch asy_d_latch_4 (.RST(in_17), .CLK(in_4), .D(out_21), .nQ(out_21));  // open: Q
  Asy_D_latch asy_d_latch_5 (.RST(in_17), .CLK(in_5), .D(out_22), .nQ(out_22));  // open: Q
  Asy_D_latch asy_d_latch_6 (.RST(in_17), .CLK(in_6), .D(out_23), .nQ(out_23));  // open: Q
  Asy_D_latch asy_d_latch_7 (.RST(in_17), .CLK(in_7), .D(out_24), .nQ(out_24));  // open: Q
  Asy_D_latch asy_d_latch_8 (.RST(in_17), .CLK(in_8), .D(out_25), .nQ(out_25));  // open: Q
  Asy_D_latch asy_d_latch_9 (.RST(in_17), .CLK(in_9), .D(out_26), .nQ(out_26));  // open: Q
  Asy_D_latch asy_d_latch_10 (.RST(in_17), .CLK(in_10), .D(out_27), .nQ(out_27));  // open: Q
  Asy_D_latch asy_d_latch_11 (.RST(in_17), .CLK(in_11), .D(out_28), .nQ(out_28));  // open: Q
  Asy_D_latch asy_d_latch_12 (.RST(in_17), .CLK(in_12), .D(out_29), .nQ(out_29));  // open: Q
  Asy_D_latch asy_d_latch_13 (.RST(in_17), .CLK(in_13), .D(out_30), .nQ(out_30));  // open: Q
  Asy_D_latch asy_d_latch_14 (.RST(in_17), .CLK(in_14), .D(out_31), .nQ(out_31));  // open: Q
  Asy_D_latch asy_d_latch_15 (.RST(in_17), .CLK(in_15), .D(out_32), .nQ(out_32));  // open: Q
  Asy_D_latch asy_d_latch_16 (.RST(in_17), .CLK(in_16), .D(out_33), .nQ(out_33));  // open: Q
endmodule

module Asy_D_latch (
  input  RST,
  input  CLK,
  input  D,
  output Q,
  output nQ
);

  wire asy_d_ff_1_out_4, not_1_out;

  not not_1 (not_1_out, CLK);
  Asy_D_FF asy_d_ff_1 (.RST(RST), .CLK(not_1_out), .D(D), .out_4(asy_d_ff_1_out_4));  // open: out_5
  Asy_D_FF asy_d_ff_2 (.RST(RST), .CLK(CLK), .D(asy_d_ff_1_out_4), .out_4(Q), .out_5(nQ));
endmodule

module Asy_D_FF (
  input  RST,
  input  CLK,
  input  D,
  output out_4,
  output out_5
);

  wire and_1_out, and_2_out, and_3_out, not_1_out, not_2_out, or_1_out;

  not not_1 (not_1_out, RST);
  not not_2 (not_2_out, D);
  and and_1 (and_1_out, CLK, not_2_out);
  and and_2 (and_2_out, CLK, D);
  and and_3 (and_3_out, not_1_out, and_1_out);
  or or_1 (or_1_out, ~not_1_out, and_2_out);  // OR_Gate
  SR_latch sr_latch_1 (.in_1(and_3_out), .in_2(or_1_out), .out_3(out_4), .out_4(out_5));
endmodule

module SR_latch (
  input  in_1,
  input  in_2,
  output out_3,
  output out_4
);

  nor nor_1 (out_3, in_1, out_4);
  nor nor_2 (out_4, out_3, in_2);
endmodule

module calculate_part1 (
  input  i1,
  input  i2,
  input  i3,
  input  i4,
  input  i5,
  input  i6,
  input  i7,
  input  i8,
  input  i9,
  input  i10,
  input  i11,
  input  i12,
  output o1,
  output o2,
  output o3,
  output o4,
  output o5,
  output o6,
  output o7,
  output o8
);

  wire and_1_out, and_2_out, and_3_out, and_4_out, and_5_out, and_6_out, and_7_out, and_8_out, and_9_out,
       and_10_out, and_11_out, and_12_out, and_13_out, and_14_out, and_15_out, and_16_out, and_17_out,
       and_18_out, and_19_out, and_20_out, and_21_out, and_22_out, and_23_out, and_24_out, and_25_out,
       and_26_out, and_27_out, and_28_out, and_29_out, and_30_out, and_31_out, and_32_out, and_33_out,
       and_34_out, and_35_out, and_36_out, and_37_out, and_38_out, and_39_out, and_40_out, and_41_out,
       and_42_out, and_43_out, and_44_out, and_45_out, and_46_out, and_47_out, and_48_out, and_49_out,
       and_50_out, and_51_out, and_52_out, and_53_out, and_54_out, and_55_out, and_56_out, and_57_out,
       and_58_out, and_59_out, and_60_out, and_61_out, and_62_out, and_63_out, and_64_out, and_65_out,
       and_66_out, and_67_out, and_68_out, and_69_out, and_70_out, and_71_out, and_72_out, not_1_out,
       not_2_out, not_3_out, not_4_out, not_5_out, not_6_out, not_7_out, not_8_out, not_9_out, not_10_out,
       not_11_out, not_12_out, not_13_out, not_14_out, not_15_out, not_16_out, not_17_out, not_18_out,
       not_19_out, not_20_out, not_21_out, not_22_out, not_23_out, not_24_out, not_25_out, not_26_out,
       not_27_out, not_28_out, not_29_out, not_30_out, not_31_out, not_32_out, not_33_out, not_34_out,
       not_35_out, not_36_out, not_37_out, not_38_out, not_39_out, not_40_out, not_41_out, not_42_out,
       not_43_out, not_44_out, not_45_out, not_46_out, not_47_out, not_48_out, not_49_out, not_50_out,
       not_51_out, not_52_out, not_53_out, not_54_out, not_55_out, not_56_out, not_57_out, not_58_out,
       not_59_out, not_60_out, not_61_out, not_62_out, not_63_out, not_64_out, not_65_out, not_66_out,
       not_67_out, not_68_out, not_69_out, not_70_out, not_71_out, not_72_out, not_73_out, not_74_out,
       not_75_out, not_76_out, not_77_out, not_78_out, not_79_out, not_80_out, not_81_out, not_82_out,
       not_83_out, not_84_out, not_85_out, not_86_out, not_87_out, not_88_out, not_89_out, not_90_out,
       not_91_out, not_92_out, not_93_out, not_94_out, not_95_out, not_96_out, not_97_out, not_98_out,
       not_99_out, not_100_out, not_101_out, not_102_out, not_103_out, not_104_out, not_105_out, not_106_out,
       not_107_out, not_108_out, not_109_out, not_110_out, not_111_out, not_112_out, not_113_out,
       not_114_out, not_115_out, not_116_out, not_117_out, not_118_out, not_119_out, not_120_out,
       not_121_out, not_122_out, not_123_out, not_124_out, not_125_out, not_126_out, not_127_out,
       not_128_out, not_129_out, not_130_out, not_131_out, not_132_out, not_133_out, not_134_out,
       not_135_out, not_136_out, not_137_out, not_138_out, not_139_out, not_140_out, not_141_out,
       not_142_out, not_143_out, not_144_out, not_145_out, not_146_out, not_147_out, not_148_out,
       not_149_out, not_150_out, not_151_out, not_152_out, not_153_out, not_154_out, not_155_out, not_156_out;

  not not_1 (not_1_out, i2);
  and and_1 (and_1_out, i1, not_1_out, not_2_out);
  not not_2 (not_2_out, i5);
  not not_3 (not_3_out, i1);
  and and_2 (and_2_out, not_3_out, i2, not_4_out);
  not not_4 (not_4_out, i5);
  not not_5 (not_5_out, i1);
  and and_3 (and_3_out, not_5_out, not_6_out, i5);
  not not_6 (not_6_out, i2);
  and and_4 (and_4_out, i1, i2, i5);
  not not_7 (not_7_out, i2);
  not not_8 (not_8_out, i3);
  not not_9 (not_9_out, i6);
  not not_10 (not_10_out, i1);
  not not_11 (not_11_out, i3);
  not not_12 (not_12_out, i6);
  not not_13 (not_13_out, i1);
  not not_14 (not_14_out, i2);
  not not_15 (not_15_out, i6);
  not not_16 (not_16_out, i1);
  not not_17 (not_17_out, i2);
  not not_18 (not_18_out, i3);
  not not_19 (not_19_out, i1);
  not not_20 (not_20_out, i2);
  not not_21 (not_21_out, i3);
  not not_22 (not_22_out, i6);
  not not_23 (not_23_out, i2);
  not not_24 (not_24_out, i3);
  not not_25 (not_25_out, i7);
  not not_26 (not_26_out, i4);
  not not_27 (not_27_out, i3);
  not not_28 (not_28_out, i7);
  not not_29 (not_29_out, i4);
  not not_30 (not_30_out, i2);
  not not_31 (not_31_out, i7);
  not not_32 (not_32_out, i4);
  not not_33 (not_33_out, i2);
  not not_34 (not_34_out, i3);
  not not_35 (not_35_out, i4);
  not not_36 (not_36_out, i2);
  not not_37 (not_37_out, i3);
  not not_38 (not_38_out, i7);
  and and_5 (and_5_out, i4, i3, i8);
  not not_39 (not_39_out, i4);
  and and_6 (and_6_out, not_39_out, not_40_out, i8);
  not not_40 (not_40_out, i3);
  not not_41 (not_41_out, i4);
  and and_7 (and_7_out, not_41_out, i3, not_42_out);
  not not_42 (not_42_out, i8);
  and and_8 (and_8_out, i4, not_43_out, not_44_out);
  not not_43 (not_43_out, i3);
  not not_44 (not_44_out, i8);
  not not_45 (not_45_out, i5);
  not not_46 (not_46_out, i6);
  not not_47 (not_47_out, i9);
  not not_48 (not_48_out, i1);
  not not_49 (not_49_out, i6);
  not not_50 (not_50_out, i9);
  not not_51 (not_51_out, i1);
  not not_52 (not_52_out, i5);
  not not_53 (not_53_out, i9);
  not not_54 (not_54_out, i1);
  not not_55 (not_55_out, i5);
  not not_56 (not_56_out, i6);
  not not_57 (not_57_out, i1);
  not not_58 (not_58_out, i5);
  not not_59 (not_59_out, i6);
  not not_60 (not_60_out, i9);
  not not_61 (not_61_out, i5);
  not not_62 (not_62_out, i6);
  not not_63 (not_63_out, i7);
  not not_64 (not_64_out, i10);
  not not_65 (not_65_out, i2);
  not not_66 (not_66_out, i6);
  not not_67 (not_67_out, i7);
  not not_68 (not_68_out, i10);
  not not_69 (not_69_out, i2);
  not not_70 (not_70_out, i5);
  not not_71 (not_71_out, i7);
  not not_72 (not_72_out, i10);
  not not_73 (not_73_out, i2);
  not not_74 (not_74_out, i5);
  not not_75 (not_75_out, i6);
  not not_76 (not_76_out, i10);
  not not_77 (not_77_out, i2);
  not not_78 (not_78_out, i5);
  not not_79 (not_79_out, i6);
  not not_80 (not_80_out, i7);
  not not_81 (not_81_out, i2);
  not not_82 (not_82_out, i5);
  not not_83 (not_83_out, i2);
  not not_84 (not_84_out, i6);
  not not_85 (not_85_out, i2);
  not not_86 (not_86_out, i7);
  not not_87 (not_87_out, i2);
  not not_88 (not_88_out, i10);
  not not_89 (not_89_out, i5);
  not not_90 (not_90_out, i6);
  not not_91 (not_91_out, i5);
  not not_92 (not_92_out, i7);
  not not_93 (not_93_out, i5);
  not not_94 (not_94_out, i10);
  not not_95 (not_95_out, i6);
  not not_96 (not_96_out, i7);
  not not_97 (not_97_out, i6);
  not not_98 (not_98_out, i10);
  not not_99 (not_99_out, i7);
  not not_100 (not_100_out, i10);
  not not_101 (not_101_out, i8);
  not not_102 (not_102_out, i6);
  not not_103 (not_103_out, i7);
  not not_104 (not_104_out, i11);
  not not_105 (not_105_out, i3);
  not not_106 (not_106_out, i6);
  not not_107 (not_107_out, i7);
  not not_108 (not_108_out, i11);
  not not_109 (not_109_out, i3);
  not not_110 (not_110_out, i8);
  not not_111 (not_111_out, i7);
  not not_112 (not_112_out, i10);
  not not_113 (not_113_out, i3);
  not not_114 (not_114_out, i8);
  not not_115 (not_115_out, i6);
  not not_116 (not_116_out, i11);
  not not_117 (not_117_out, i3);
  not not_118 (not_118_out, i8);
  not not_119 (not_119_out, i6);
  not not_120 (not_120_out, i7);
  not not_121 (not_121_out, i3);
  not not_122 (not_122_out, i8);
  not not_123 (not_123_out, i3);
  not not_124 (not_124_out, i6);
  not not_125 (not_125_out, i3);
  not not_126 (not_126_out, i7);
  not not_127 (not_127_out, i3);
  not not_128 (not_128_out, i11);
  not not_129 (not_129_out, i8);
  not not_130 (not_130_out, i6);
  not not_131 (not_131_out, i8);
  not not_132 (not_132_out, i7);
  not not_133 (not_133_out, i8);
  not not_134 (not_134_out, i11);
  not not_135 (not_135_out, i6);
  not not_136 (not_136_out, i7);
  not not_137 (not_137_out, i6);
  not not_138 (not_138_out, i11);
  not not_139 (not_139_out, i7);
  not not_140 (not_140_out, i11);
  not not_141 (not_141_out, i7);
  not not_142 (not_142_out, i8);
  not not_143 (not_143_out, i12);
  not not_144 (not_144_out, i4);
  not not_145 (not_145_out, i8);
  not not_146 (not_146_out, i12);
  not not_147 (not_147_out, i4);
  not not_148 (not_148_out, i7);
  not not_149 (not_149_out, i12);
  not not_150 (not_150_out, i4);
  not not_151 (not_151_out, i7);
  not not_152 (not_152_out, i8);
  not not_153 (not_153_out, i4);
  not not_154 (not_154_out, i7);
  not not_155 (not_155_out, i8);
  not not_156 (not_156_out, i12);
  or or_1 (o1, and_1_out, and_2_out, and_3_out, and_4_out);
  and and_9 (and_9_out, i1, not_7_out, not_8_out, not_9_out);
  and and_10 (and_10_out, not_10_out, i2, not_11_out, not_12_out);
  and and_11 (and_11_out, not_13_out, not_14_out, i3, not_15_out);
  and and_12 (and_12_out, not_16_out, not_17_out, not_18_out, i6);
  and and_13 (and_13_out, not_19_out, i2, i3, i6);
  and and_14 (and_14_out, i1, not_20_out, i3, i6);
  and and_15 (and_15_out, i1, i2, not_21_out, i6);
  and and_16 (and_16_out, i1, i2, i3, not_22_out);
  and and_17 (and_17_out, i4, not_23_out, not_24_out, not_25_out);
  and and_18 (and_18_out, not_26_out, i2, not_27_out, not_28_out);
  and and_19 (and_19_out, not_29_out, not_30_out, i3, not_31_out);
  and and_20 (and_20_out, not_32_out, not_33_out, not_34_out, i7);
  and and_21 (and_21_out, not_35_out, i2, i3, i7);
  and and_22 (and_22_out, i4, not_36_out, i3, i7);
  and and_23 (and_23_out, i4, i2, not_37_out, i7);
  and and_24 (and_24_out, i4, i2, i3, not_38_out);
  or or_2 (o4, and_5_out, and_6_out, and_7_out, and_8_out);
  and and_25 (and_25_out, i1, not_45_out, not_46_out, not_47_out);
  and and_26 (and_26_out, not_48_out, i5, not_49_out, not_50_out);
  and and_27 (and_27_out, not_51_out, not_52_out, i6, not_53_out);
  and and_28 (and_28_out, not_54_out, not_55_out, not_56_out, i9);
  and and_29 (and_29_out, not_57_out, i5, i6, i9);
  and and_30 (and_30_out, i1, not_58_out, i6, i9);
  and and_31 (and_31_out, i1, i5, not_59_out, i9);
  and and_32 (and_32_out, i1, i5, i6, not_60_out);
  and and_33 (and_33_out, i2, not_61_out, not_62_out, not_63_out, not_64_out);
  and and_34 (and_34_out, not_65_out, i5, not_66_out, not_67_out, not_68_out);
  and and_35 (and_35_out, not_69_out, not_70_out, i6, not_71_out, not_72_out);
  and and_36 (and_36_out, not_73_out, not_74_out, not_75_out, i7, not_76_out);
  and and_37 (and_37_out, not_77_out, not_78_out, not_79_out, not_80_out, i10);
  and and_38 (and_38_out, not_81_out, not_82_out, i6, i7, i10);
  and and_39 (and_39_out, not_83_out, i5, not_84_out, i7, i10);
  and and_40 (and_40_out, not_85_out, i5, i6, not_86_out, i10);
  and and_41 (and_41_out, not_87_out, i5, i6, i7, not_88_out);
  and and_42 (and_42_out, i2, not_89_out, not_90_out, i7, i10);
  and and_43 (and_43_out, i2, not_91_out, i6, not_92_out, i10);
  and and_44 (and_44_out, i2, not_93_out, i6, i7, not_94_out);
  and and_45 (and_45_out, i2, i5, not_95_out, not_96_out, i10);
  and and_46 (and_46_out, i2, i5, not_97_out, i7, not_98_out);
  and and_47 (and_47_out, i2, i5, i6, not_99_out, not_100_out);
  and and_48 (and_48_out, i2, i5, i6, i7, i10);
  and and_49 (and_49_out, i3, not_101_out, not_102_out, not_103_out, not_104_out);
  and and_50 (and_50_out, not_105_out, i8, not_106_out, not_107_out, not_108_out);
  and and_51 (and_51_out, not_109_out, not_110_out, i6, not_111_out, not_112_out);
  and and_52 (and_52_out, not_113_out, not_114_out, not_115_out, i7, not_116_out);
  and and_53 (and_53_out, not_117_out, not_118_out, not_119_out, not_120_out, i11);
  and and_54 (and_54_out, not_121_out, not_122_out, i6, i7, i11);
  and and_55 (and_55_out, not_123_out, i8, not_124_out, i7, i11);
  and and_56 (and_56_out, not_125_out, i8, i6, not_126_out, i11);
  and and_57 (and_57_out, not_127_out, i8, i6, i7, not_128_out);
  and and_58 (and_58_out, i3, not_129_out, not_130_out, i7, i11);
  and and_59 (and_59_out, i3, not_131_out, i6, not_132_out, i11);
  and and_60 (and_60_out, i3, not_133_out, i6, i7, not_134_out);
  and and_61 (and_61_out, i3, i8, not_135_out, not_136_out, i11);
  and and_62 (and_62_out, i3, i8, not_137_out, i7, not_138_out);
  and and_63 (and_63_out, i3, i8, i6, not_139_out, not_140_out);
  and and_64 (and_64_out, i3, i8, i6, i7, i11);
  and and_65 (and_65_out, i4, not_141_out, not_142_out, not_143_out);
  and and_66 (and_66_out, not_144_out, i7, not_145_out, not_146_out);
  and and_67 (and_67_out, not_147_out, not_148_out, i8, not_149_out);
  and and_68 (and_68_out, not_150_out, not_151_out, not_152_out, i12);
  and and_69 (and_69_out, not_153_out, i7, i8, i12);
  and and_70 (and_70_out, i4, not_154_out, i8, i12);
  and and_71 (and_71_out, i4, i7, not_155_out, i12);
  and and_72 (and_72_out, i4, i7, i8, not_156_out);
  or or_3 (o2, and_9_out, and_10_out, and_11_out, and_12_out, and_13_out, and_14_out, and_15_out, and_16_out);
  or or_4 (o3, and_17_out, and_18_out, and_19_out, and_20_out, and_21_out, and_22_out, and_23_out, and_24_out);
  or or_5 (o5, and_25_out, and_26_out, and_27_out, and_28_out, and_29_out, and_30_out, and_31_out, and_32_out);
  or or_6 (o6, and_33_out, and_34_out, and_35_out, and_36_out, and_37_out, and_38_out, and_39_out, and_40_out, and_41_out, and_42_out, and_43_out, and_44_out, and_45_out, and_46_out, and_47_out, and_48_out);
  or or_7 (o7, and_49_out, and_50_out, and_51_out, and_52_out, and_53_out, and_54_out, and_55_out, and_56_out, and_57_out, and_58_out, and_59_out, and_60_out, and_61_out, and_62_out, and_63_out, and_64_out);
  or or_8 (o8, and_65_out, and_66_out, and_67_out, and_68_out, and_69_out, and_70_out, and_71_out, and_72_out);
endmodule

module calculate_part2 (
  input  i5,
  input  i6,
  input  i7,
  input  i8,
  input  i9,
  input  i10,
  input  i11,
  input  i12,
  input  i13,
  input  i14,
  input  i15,
  input  i16,
  output o9,
  output o10,
  output o11,
  output o12,
  output o13,
  output o14,
  output o15,
  output o16
);

  wire and_1_out, and_2_out, and_3_out, and_4_out, and_5_out, and_6_out, and_7_out, and_8_out, and_9_out,
       and_10_out, and_11_out, and_12_out, and_13_out, and_14_out, and_15_out, and_16_out, and_17_out,
       and_18_out, and_19_out, and_20_out, and_21_out, and_22_out, and_23_out, and_24_out, and_25_out,
       and_26_out, and_27_out, and_28_out, and_29_out, and_30_out, and_31_out, and_32_out, and_33_out,
       and_34_out, and_35_out, and_36_out, and_37_out, and_38_out, and_39_out, and_40_out, and_41_out,
       and_42_out, and_43_out, and_44_out, and_45_out, and_46_out, and_47_out, and_48_out, and_49_out,
       and_50_out, and_51_out, and_52_out, and_53_out, and_54_out, and_55_out, and_56_out, and_57_out,
       and_58_out, and_59_out, and_60_out, and_61_out, and_62_out, and_63_out, and_64_out, and_65_out,
       and_66_out, and_67_out, and_68_out, and_69_out, and_70_out, and_71_out, and_72_out, not_1_out,
       not_2_out, not_3_out, not_4_out, not_5_out, not_6_out, not_7_out, not_8_out, not_9_out, not_10_out,
       not_11_out, not_12_out, not_13_out, not_14_out, not_15_out, not_16_out, not_17_out, not_18_out,
       not_19_out, not_20_out, not_21_out, not_22_out, not_23_out, not_24_out, not_25_out, not_26_out,
       not_27_out, not_28_out, not_29_out, not_30_out, not_31_out, not_32_out, not_33_out, not_34_out,
       not_35_out, not_36_out, not_37_out, not_38_out, not_39_out, not_40_out, not_41_out, not_42_out,
       not_43_out, not_44_out, not_45_out, not_46_out, not_47_out, not_48_out, not_49_out, not_50_out,
       not_51_out, not_52_out, not_53_out, not_54_out, not_55_out, not_56_out, not_57_out, not_58_out,
       not_59_out, not_60_out, not_61_out, not_62_out, not_63_out, not_64_out, not_65_out, not_66_out,
       not_67_out, not_68_out, not_69_out, not_70_out, not_71_out, not_72_out, not_73_out, not_74_out,
       not_75_out, not_76_out, not_77_out, not_78_out, not_79_out, not_80_out, not_81_out, not_82_out,
       not_83_out, not_84_out, not_85_out, not_86_out, not_87_out, not_88_out, not_89_out, not_90_out,
       not_91_out, not_92_out, not_93_out, not_94_out, not_95_out, not_96_out, not_97_out, not_98_out,
       not_99_out, not_100_out, not_101_out, not_102_out, not_103_out, not_104_out, not_105_out, not_106_out,
       not_107_out, not_108_out, not_109_out, not_110_out, not_111_out, not_112_out, not_113_out,
       not_114_out, not_115_out, not_116_out, not_117_out, not_118_out, not_119_out, not_120_out,
       not_121_out, not_122_out, not_123_out, not_124_out, not_125_out, not_126_out, not_127_out,
       not_128_out, not_129_out, not_130_out, not_131_out, not_132_out, not_133_out, not_134_out,
       not_135_out, not_136_out, not_137_out, not_138_out, not_139_out, not_140_out, not_141_out,
       not_142_out, not_143_out, not_144_out, not_145_out, not_146_out, not_147_out, not_148_out,
       not_149_out, not_150_out, not_151_out, not_152_out, not_153_out, not_154_out, not_155_out, not_156_out;

  not not_1 (not_1_out, i10);
  not not_2 (not_2_out, i9);
  not not_3 (not_3_out, i5);
  not not_4 (not_4_out, i13);
  not not_5 (not_5_out, i9);
  not not_6 (not_6_out, i5);
  not not_7 (not_7_out, i13);
  not not_8 (not_8_out, i10);
  not not_9 (not_9_out, i5);
  not not_10 (not_10_out, i13);
  not not_11 (not_11_out, i10);
  not not_12 (not_12_out, i9);
  not not_13 (not_13_out, i13);
  not not_14 (not_14_out, i10);
  not not_15 (not_15_out, i9);
  not not_16 (not_16_out, i5);
  not not_17 (not_17_out, i9);
  not not_18 (not_18_out, i6);
  not not_19 (not_19_out, i11);
  not not_20 (not_20_out, i10);
  not not_21 (not_21_out, i14);
  not not_22 (not_22_out, i6);
  not not_23 (not_23_out, i11);
  not not_24 (not_24_out, i10);
  not not_25 (not_25_out, i14);
  not not_26 (not_26_out, i9);
  not not_27 (not_27_out, i11);
  not not_28 (not_28_out, i10);
  not not_29 (not_29_out, i14);
  not not_30 (not_30_out, i9);
  not not_31 (not_31_out, i6);
  not not_32 (not_32_out, i10);
  not not_33 (not_33_out, i14);
  not not_34 (not_34_out, i9);
  not not_35 (not_35_out, i6);
  not not_36 (not_36_out, i11);
  not not_37 (not_37_out, i14);
  not not_38 (not_38_out, i9);
  not not_39 (not_39_out, i14);
  not not_40 (not_40_out, i6);
  not not_41 (not_41_out, i14);
  not not_42 (not_42_out, i11);
  not not_43 (not_43_out, i14);
  not not_44 (not_44_out, i10);
  not not_45 (not_45_out, i9);
  not not_46 (not_46_out, i6);
  not not_47 (not_47_out, i9);
  not not_48 (not_48_out, i11);
  not not_49 (not_49_out, i9);
  not not_50 (not_50_out, i10);
  not not_51 (not_51_out, i6);
  not not_52 (not_52_out, i11);
  not not_53 (not_53_out, i6);
  not not_54 (not_54_out, i10);
  not not_55 (not_55_out, i11);
  not not_56 (not_56_out, i10);
  not not_57 (not_57_out, i12);
  not not_58 (not_58_out, i7);
  not not_59 (not_59_out, i11);
  not not_60 (not_60_out, i10);
  not not_61 (not_61_out, i15);
  not not_62 (not_62_out, i7);
  not not_63 (not_63_out, i11);
  not not_64 (not_64_out, i10);
  not not_65 (not_65_out, i15);
  not not_66 (not_66_out, i12);
  not not_67 (not_67_out, i11);
  not not_68 (not_68_out, i10);
  not not_69 (not_69_out, i15);
  not not_70 (not_70_out, i12);
  not not_71 (not_71_out, i7);
  not not_72 (not_72_out, i10);
  not not_73 (not_73_out, i15);
  not not_74 (not_74_out, i12);
  not not_75 (not_75_out, i7);
  not not_76 (not_76_out, i11);
  not not_77 (not_77_out, i15);
  not not_78 (not_78_out, i12);
  not not_79 (not_79_out, i15);
  not not_80 (not_80_out, i7);
  not not_81 (not_81_out, i15);
  not not_82 (not_82_out, i11);
  not not_83 (not_83_out, i15);
  not not_84 (not_84_out, i10);
  not not_85 (not_85_out, i12);
  not not_86 (not_86_out, i7);
  not not_87 (not_87_out, i12);
  not not_88 (not_88_out, i11);
  not not_89 (not_89_out, i12);
  not not_90 (not_90_out, i10);
  not not_91 (not_91_out, i7);
  not not_92 (not_92_out, i11);
  not not_93 (not_93_out, i7);
  not not_94 (not_94_out, i10);
  not not_95 (not_95_out, i11);
  not not_96 (not_96_out, i10);
  not not_97 (not_97_out, i11);
  not not_98 (not_98_out, i8);
  not not_99 (not_99_out, i12);
  not not_100 (not_100_out, i16);
  not not_101 (not_101_out, i8);
  not not_102 (not_102_out, i12);
  not not_103 (not_103_out, i16);
  not not_104 (not_104_out, i11);
  not not_105 (not_105_out, i12);
  not not_106 (not_106_out, i16);
  not not_107 (not_107_out, i11);
  not not_108 (not_108_out, i8);
  not not_109 (not_109_out, i16);
  not not_110 (not_110_out, i11);
  not not_111 (not_111_out, i8);
  not not_112 (not_112_out, i12);
  not not_113 (not_113_out, i13);
  and and_1 (and_1_out, i9, not_113_out, not_114_out);
  not not_114 (not_114_out, i14);
  not not_115 (not_115_out, i9);
  and and_2 (and_2_out, not_115_out, i13, not_116_out);
  not not_116 (not_116_out, i14);
  not not_117 (not_117_out, i9);
  and and_3 (and_3_out, not_117_out, not_118_out, i14);
  not not_118 (not_118_out, i13);
  and and_4 (and_4_out, i9, i13, i14);
  not not_119 (not_119_out, i10);
  not not_120 (not_120_out, i14);
  not not_121 (not_121_out, i15);
  not not_122 (not_122_out, i13);
  not not_123 (not_123_out, i14);
  not not_124 (not_124_out, i15);
  not not_125 (not_125_out, i13);
  not not_126 (not_126_out, i10);
  not not_127 (not_127_out, i15);
  not not_128 (not_128_out, i13);
  not not_129 (not_129_out, i10);
  not not_130 (not_130_out, i14);
  not not_131 (not_131_out, i13);
  not not_132 (not_132_out, i10);
  not not_133 (not_133_out, i14);
  not not_134 (not_134_out, i15);
  not not_135 (not_135_out, i11);
  not not_136 (not_136_out, i14);
  not not_137 (not_137_out, i15);
  not not_138 (not_138_out, i16);
  not not_139 (not_139_out, i14);
  not not_140 (not_140_out, i15);
  not not_141 (not_141_out, i16);
  not not_142 (not_142_out, i11);
  not not_143 (not_143_out, i15);
  not not_144 (not_144_out, i16);
  not not_145 (not_145_out, i11);
  not not_146 (not_146_out, i14);
  not not_147 (not_147_out, i16);
  not not_148 (not_148_out, i11);
  not not_149 (not_149_out, i14);
  not not_150 (not_150_out, i15);
  and and_5 (and_5_out, i12, not_151_out, not_152_out);
  not not_151 (not_151_out, i16);
  not not_152 (not_152_out, i15);
  not not_153 (not_153_out, i12);
  and and_6 (and_6_out, not_153_out, i16, not_154_out);
  not not_154 (not_154_out, i15);
  not not_155 (not_155_out, i12);
  and and_7 (and_7_out, not_155_out, not_156_out, i15);
  not not_156 (not_156_out, i16);
  and and_8 (and_8_out, i12, i16, i15);
  and and_9 (and_9_out, i13, not_1_out, not_2_out, not_3_out);
  and and_10 (and_10_out, not_4_out, i10, not_5_out, not_6_out);
  and and_11 (and_11_out, not_7_out, not_8_out, i9, not_9_out);
  and and_12 (and_12_out, not_10_out, not_11_out, not_12_out, i5);
  and and_13 (and_13_out, not_13_out, i10, i9, i5);
  and and_14 (and_14_out, i13, not_14_out, i9, i5);
  and and_15 (and_15_out, i13, i10, not_15_out, i5);
  and and_16 (and_16_out, i13, i10, i9, not_16_out);
  and and_17 (and_17_out, i14, not_17_out, not_18_out, not_19_out, not_20_out);
  and and_18 (and_18_out, not_21_out, i9, not_22_out, not_23_out, not_24_out);
  and and_19 (and_19_out, not_25_out, not_26_out, i6, not_27_out, not_28_out);
  and and_20 (and_20_out, not_29_out, not_30_out, not_31_out, i11, not_32_out);
  and and_21 (and_21_out, not_33_out, not_34_out, not_35_out, not_36_out, i10);
  and and_22 (and_22_out, not_37_out, not_38_out, i6, i11, i10);
  and and_23 (and_23_out, not_39_out, i9, not_40_out, i11, i10);
  and and_24 (and_24_out, not_41_out, i9, i6, not_42_out, i10);
  and and_25 (and_25_out, not_43_out, i9, i6, i11, not_44_out);
  and and_26 (and_26_out, i14, not_45_out, not_46_out, i11, i10);
  and and_27 (and_27_out, i14, not_47_out, i6, not_48_out, i10);
  and and_28 (and_28_out, i14, not_49_out, i6, i11, not_50_out);
  and and_29 (and_29_out, i14, i9, not_51_out, not_52_out, i10);
  and and_30 (and_30_out, i14, i9, not_53_out, i11, not_54_out);
  and and_31 (and_31_out, i14, i9, i6, not_55_out, not_56_out);
  and and_32 (and_32_out, i14, i9, i6, i11, i10);
  and and_33 (and_33_out, i15, not_57_out, not_58_out, not_59_out, not_60_out);
  and and_34 (and_34_out, not_61_out, i12, not_62_out, not_63_out, not_64_out);
  and and_35 (and_35_out, not_65_out, not_66_out, i7, not_67_out, not_68_out);
  and and_36 (and_36_out, not_69_out, not_70_out, not_71_out, i11, not_72_out);
  and and_37 (and_37_out, not_73_out, not_74_out, not_75_out, not_76_out, i10);
  and and_38 (and_38_out, not_77_out, not_78_out, i7, i11, i10);
  and and_39 (and_39_out, not_79_out, i12, not_80_out, i11, i10);
  and and_40 (and_40_out, not_81_out, i12, i7, not_82_out, i10);
  and and_41 (and_41_out, not_83_out, i12, i7, i11, not_84_out);
  and and_42 (and_42_out, i15, not_85_out, not_86_out, i11, i10);
  and and_43 (and_43_out, i15, not_87_out, i7, not_88_out, i10);
  and and_44 (and_44_out, i15, not_89_out, i7, i11, not_90_out);
  and and_45 (and_45_out, i15, i12, not_91_out, not_92_out, i10);
  and and_46 (and_46_out, i15, i12, not_93_out, i11, not_94_out);
  and and_47 (and_47_out, i15, i12, i7, not_95_out, not_96_out);
  and and_48 (and_48_out, i15, i12, i7, i11, i10);
  and and_49 (and_49_out, i16, not_97_out, not_98_out, not_99_out);
  and and_50 (and_50_out, not_100_out, i11, not_101_out, not_102_out);
  and and_51 (and_51_out, not_103_out, not_104_out, i8, not_105_out);
  and and_52 (and_52_out, not_106_out, not_107_out, not_108_out, i12);
  and and_53 (and_53_out, not_109_out, i11, i8, i12);
  and and_54 (and_54_out, i16, not_110_out, i8, i12);
  and and_55 (and_55_out, i16, i11, not_111_out, i12);
  and and_56 (and_56_out, i16, i11, i8, not_112_out);
  or or_1 (o13, and_1_out, and_2_out, and_3_out, and_4_out);
  and and_57 (and_57_out, i13, not_119_out, not_120_out, not_121_out);
  and and_58 (and_58_out, not_122_out, i10, not_123_out, not_124_out);
  and and_59 (and_59_out, not_125_out, not_126_out, i14, not_127_out);
  and and_60 (and_60_out, not_128_out, not_129_out, not_130_out, i15);
  and and_61 (and_61_out, not_131_out, i10, i14, i15);
  and and_62 (and_62_out, i13, not_132_out, i14, i15);
  and and_63 (and_63_out, i13, i10, not_133_out, i15);
  and and_64 (and_64_out, i13, i10, i14, not_134_out);
  and and_65 (and_65_out, i16, not_135_out, not_136_out, not_137_out);
  and and_66 (and_66_out, not_138_out, i11, not_139_out, not_140_out);
  and and_67 (and_67_out, not_141_out, not_142_out, i14, not_143_out);
  and and_68 (and_68_out, not_144_out, not_145_out, not_146_out, i15);
  and and_69 (and_69_out, not_147_out, i11, i14, i15);
  and and_70 (and_70_out, i16, not_148_out, i14, i15);
  and and_71 (and_71_out, i16, i11, not_149_out, i15);
  and and_72 (and_72_out, i16, i11, i14, not_150_out);
  or or_2 (o16, and_5_out, and_6_out, and_7_out, and_8_out);
  or or_3 (o9, and_9_out, and_10_out, and_11_out, and_12_out, and_13_out, and_14_out, and_15_out, and_16_out);
  or or_4 (o10, and_17_out, and_18_out, and_19_out, and_20_out, and_21_out, and_22_out, and_23_out, and_24_out, and_25_out, and_26_out, and_27_out, and_28_out, and_29_out, and_30_out, and_31_out, and_32_out);
  or or_5 (o11, and_33_out, and_34_out, and_35_out, and_36_out, and_37_out, and_38_out, and_39_out, and_40_out, and_41_out, and_42_out, and_43_out, and_44_out, and_45_out, and_46_out, and_47_out, and_48_out);
  or or_6 (o12, and_49_out, and_50_out, and_51_out, and_52_out, and_53_out, and_54_out, and_55_out, and_56_out);
  or or_7 (o14, and_57_out, and_58_out, and_59_out, and_60_out, and_61_out, and_62_out, and_63_out, and_64_out);
  or or_8 (o15, and_65_out, and_66_out, and_67_out, and_68_out, and_69_out, and_70_out, and_71_out, and_72_out);
endmodule
